// Logisim project adder.circ as structural Verilog: 1 circuit, main circuit main
module main (
);

  wire A, a_b_out, and_1_out, aXOb_out, B, C, carry, sum;

  xor aXOb (aXOb_out, A, B);
  and a_b (a_b_out, A, B);
  xor xor_1 (sum, aXOb_out, C);
  and and_1 (and_1_out, aXOb_out, C);
  or or_1 (carry, a_b_out, and_1_out);
endmodule
