// Logisim project alu.circ as structural Verilog: 2 circuits, main circuit main
module main (
);

  wire A0, A1, A2, and_1_out, B0, B1, B2, C0, C1, C2, C2_out, CIN, or_4_out, P0G0_g, P0G0_p, P0P1CIN_out,
       P1G0_out, P1G1_g, P1G1_p, S0, S1;
  wire [2:0] and_2_out, not_1_out, or_1_out, P0G0_sum;

  Carry P0G0 (.Carry(CIN), .B(B0), .A(A0), .Sum(P0G0_sum[0]), .P(P0G0_p), .G(P0G0_g));
  not not_1 (not_1_out[0], A0);
  not not_2 (not_1_out[1], A1);
  not not_3 (not_1_out[2], A2);
  and and_1 (and_1_out, CIN, P0G0_p);
  and and_2 (and_2_out[0], A0, B0);
  and and_3 (and_2_out[1], A1, B1);
  and and_4 (and_2_out[2], A2, B2);
  or or_1 (or_1_out[0], A0, B0);
  or or_2 (or_1_out[1], A1, B1);
  or or_3 (or_1_out[2], A2, B2);
  or or_4 (or_4_out, and_1_out, P0G0_g);
  Carry P1G1 (.Carry(or_4_out), .B(B1), .A(A1), .Sum(P0G0_sum[1]), .P(P1G1_p), .G(P1G1_g));
  and P0P1CIN (P0P1CIN_out, P1G1_p, CIN, P0G0_p);
  and P1G0 (P1G0_out, P1G1_p, P0G0_g);
  Multiplexer #(.select(2), .width(3), .enable("false")) multiplexer_1 (
    .in0(and_2_out), .in1(or_1_out), .in2(not_1_out), .in3(P0G0_sum), .out({C2, C1, C0}), .sel({S1, S0}));
  or u_C2 (C2_out, P0P1CIN_out, P1G1_g, P1G0_out);
  Carry carry_1 (.Carry(C2_out), .B(B2), .A(A2), .Sum(P0G0_sum[2]));  // open: P, G
endmodule

module Carry (
  input  Carry,
  input  B,
  input  A,
  output Sum,
  output P,
  output G
);

  wire xor_1_out;

  xor xor_1 (xor_1_out, A, B);
  xor xor_2 (Sum, xor_1_out, Carry);
  or P0 (P, A, B);
  and and_1 (G, A, B);
endmodule
