// Logisim project bcd.circ as structural Verilog: 1 circuit, main circuit main
module main (
);

  wire _1_0_2_out, _1_0_out, _1_02_out, _1_3_2_out, _1_3_2_out_2, _1_3_out, _02_out, _3_1_out, _3_2_2_out,
       _3_2_3_out, _3_2_4_out, _3_2_out, _10_3_out, _10_out, a, b, c, d, e, f, g, n1_0_2_2_out, n1_0_2_out,
       n1_0_2_out_2, n1_0_out, n1_32_out, n2_1_0_out, n3_2_1_out, n3_2_out, n3_21_out, n10_2_out, n12_out,
       n32_out, n102_out, not_1_out, not_2_out, not_3_out, not_4_out, w0, w1, w2, w3;

  not not_1 (not_1_out, w0);
  not not_2 (not_2_out, w1);
  not not_3 (not_3_out, w2);
  not not_4 (not_4_out, w3);
  and _3_1 (_3_1_out, w3, not_2_out);
  and _1_3 (_1_3_out, w1, not_4_out);
  and _02 (_02_out, w0, w2);
  and n1_0 (n1_0_out, not_2_out, not_1_out);
  and n3_2 (n3_2_out, not_4_out, not_3_out);
  and _10_3 (_10_3_out, w1, w0, not_4_out);
  and n10_2 (n10_2_out, not_2_out, w0, not_3_out);
  and _3_2 (_3_2_out, w3, not_3_out);
  and n32 (n32_out, not_4_out, w2);
  and n3_2_1 (n3_2_1_out, not_4_out, not_3_out, not_2_out);
  and _10 (_10_out, w1, w0);
  and _3_2_2 (_3_2_2_out, w3, not_3_out);
  and n1_0_2 (n1_0_2_out, not_2_out, not_1_out, not_3_out);
  and n102 (n102_out, not_2_out, w0, w2);
  and n3_21 (n3_21_out, not_4_out, not_3_out, w1);
  and _1_0 (_1_0_out, w1, not_1_out);
  and n1_0_2_2 (n1_0_2_2_out, not_1_out, not_2_out, not_3_out);
  and _1_3_2 (_1_3_2_out, w1, not_1_out);
  and n1_0_2_dup2 (n1_0_2_out_2, not_1_out, not_2_out);
  and _3_2_3 (_3_2_3_out, w3, not_3_out);
  and n1_32 (n1_32_out, not_2_out, not_4_out, w2);
  and _1_02 (_1_02_out, w1, not_1_out, w2);
  and _3_2_4 (_3_2_4_out, w3, not_3_out);
  and _1_0_2 (_1_0_2_out, w1, not_1_out);
  and _1_3_2_dup2 (_1_3_2_out_2, w1, not_3_out);
  and n12 (n12_out, not_2_out, w2);
  and n2_1_0 (n2_1_0_out, not_3_out, not_2_out, not_1_out);
  or or_1 (a, _3_1_out, _1_3_out, _02_out, n2_1_0_out);
  or or_2 (b, n1_0_out, n3_2_out, _10_3_out, n10_2_out);
  or or_3 (c, _3_2_out, n32_out, n3_2_1_out, _10_out);
  or or_4 (d, _3_2_2_out, n1_0_2_out, n102_out, n3_21_out, _1_0_out);
  or or_5 (e, n1_0_2_2_out, _1_3_2_out);
  or or_6 (f, n1_0_2_out_2, _3_2_3_out, n1_32_out, _1_02_out);
  or or_7 (g, _3_2_4_out, _1_0_2_out, _1_3_2_out_2, n12_out);
endmodule
