// Logisim project bits.circ as structural Verilog: 1 circuit, main circuit main
module main (
);

  wire _1_s, _2_s, _4_s, x1, x2, x3, x4, x5, x6;

  BitAdder #(.width(6)) bitadder_1 (.in0({x6, x5, x4, x3, x2, x1}), .out({_4_s, _2_s, _1_s}));
endmodule
