// Logisim project func.circ as structural Verilog: 1 circuit, main circuit main
module main (
);

  wire _2_4_out, _23_out, _123_out, f1, f2, minus_12_out, n123_out, n124_out, not_1_out, not_3_out,
       not_4_out, x1, x2, x2_nx3_nx4_out, x3, x4;

  not not_1 (not_1_out, x1);
  // NOT_Gate not_2 has open pins: in=x2, out=open
  not not_3 (not_3_out, x3);
  not not_4 (not_4_out, x4);
  and x2_nx3_nx4 (x2_nx3_nx4_out, x2, not_3_out, not_4_out);
  and n124 (n124_out, not_1_out, x2, x4);
  and n123 (n123_out, not_1_out, x2, x3);
  and _123 (_123_out, x1, x2, x3);
  and _2_4 (_2_4_out, x2, not_4_out);
  and minus_12 (minus_12_out, not_1_out, x2);
  and _23 (_23_out, x2, x3);
  or or_1 (f1, x2_nx3_nx4_out, n124_out, n123_out, _123_out);
  or or_2 (f2, _2_4_out, minus_12_out, _23_out);
endmodule
