// Logisim project sec.circ as structural Verilog: 1 circuit, main circuit main
module main (
);

  wire C0, C1, C2, C3, D0, D1, D2, D3, D4, D5, D6, D7, decoder_1_out3, decoder_1_out5, decoder_1_out6,
       decoder_1_out7, decoder_1_out9, decoder_1_out10, decoder_1_out11, decoder_1_out12, odd_parity_1_out,
       odd_parity_2_out, odd_parity_3_out, odd_parity_4_out, Z0, Z1, Z2, Z3, Z4, Z5, Z6, Z7;
  wire [3:0] xor_1_out;

  xor odd_parity_1 (odd_parity_1_out, D0, D1, D3, D4, D6);
  xor odd_parity_2 (odd_parity_2_out, D0, D2, D3, D5, D6);
  xor odd_parity_3 (odd_parity_3_out, D1, D2, D3, D7);
  xor odd_parity_4 (odd_parity_4_out, D4, D5, D6, D7);
  xor xor_1 (xor_1_out[0], C0, odd_parity_1_out);
  xor xor_2 (xor_1_out[1], C1, odd_parity_2_out);
  xor xor_3 (xor_1_out[2], odd_parity_3_out, C2);
  xor xor_4 (xor_1_out[3], odd_parity_4_out, C3);
  Decoder #(.select(4)) decoder_1 (
    .out3(decoder_1_out3), .out5(decoder_1_out5), .out6(decoder_1_out6), .out7(decoder_1_out7),
    .out9(decoder_1_out9), .out10(decoder_1_out10), .out11(decoder_1_out11), .out12(decoder_1_out12),
    .sel(xor_1_out));  // open: out0, out1, out2, out4, out8, out13, out14, out15, en
  xor xor_5 (Z0, decoder_1_out3, D0);
  xor xor_6 (Z1, decoder_1_out5, D1);
  xor xor_7 (Z2, decoder_1_out6, D2);
  xor xor_8 (Z3, decoder_1_out7, D3);
  xor xor_9 (Z4, decoder_1_out9, D4);
  xor xor_10 (Z5, decoder_1_out10, D5);
  xor xor_11 (Z6, decoder_1_out11, D6);
  xor xor_12 (Z7, decoder_1_out12, D7);
endmodule
