// Logisim project 1.circ as structural Verilog: 2 circuits, main circuit main
module main (
);

  wire _15, _30, and_1_out_3, and_2_out_3, CLOCK;

  \and  and_1 (.in_1(_30), .in_2(1'b1), .out_3(and_1_out_3));
  D_Flip_Flop d_ff_1 (.clk(CLOCK), .D(and_1_out_3), .Q(_30));  // open: Qn, preset, en, reset
  D_Flip_Flop d_ff_2 (.clk(_30), .D(and_2_out_3), .Q(_15));  // open: Qn, preset, en, reset
  \and  and_2 (.in_1(_15), .in_2(1'b1), .out_3(and_2_out_3));
endmodule

module \and  (
  input  in_1,
  input  in_2,
  output out_3
);

  wire and_1_out, and_2_out, and_3_out, and_4_out;

  and and_1 (and_1_out, in_1, in_2);
  and and_2 (and_2_out, in_1, ~and_1_out);  // AND_Gate
  and and_3 (and_3_out, ~and_1_out, in_2);  // AND_Gate
  not not_1 (out_3, and_4_out);
  and and_4 (and_4_out, ~and_2_out, ~and_3_out);  // AND_Gate
endmodule
