// Logisim project 2.circ as structural Verilog: 1 circuit, main circuit main
module main (
);

  wire and_1_out, and_2_out, CLK, not_1_out, not_2_out, not_3_out, or_1_out, Q, R, S;

  not not_1 (not_1_out, R);
  not not_2 (not_2_out, Q);
  not not_3 (not_3_out, S);
  and and_1 (and_1_out, S, not_1_out, not_2_out);
  and and_2 (and_2_out, Q, not_3_out, R);
  T_Flip_Flop t_ff_1 (.clk(CLK), .T(or_1_out), .Q(Q));  // open: Qn, preset, reset, en
  or or_1 (or_1_out, and_1_out, and_2_out);
endmodule
