// Logisim project 3.circ as structural Verilog: 1 circuit, main circuit main
module main (
);

  wire and_1_out, and_2_out, CLK, J, K, not_1_out, not_2_out, or_1_out, Q;

  not not_1 (not_1_out, Q);
  not not_2 (not_2_out, K);
  and and_1 (and_1_out, not_1_out, J);
  and and_2 (and_2_out, Q, not_2_out);
  D_Flip_Flop d_ff_1 (.clk(CLK), .D(or_1_out), .Q(Q));  // open: Qn, preset, en, reset
  or or_1 (or_1_out, and_1_out, and_2_out);
endmodule
