// Logisim project 4.circ as structural Verilog: 3 circuits, main circuit main
module main (
);

  wire and_1_out, and_2_out, and_3_out, Carry, CLK, D0, D1, D2, D3, Enable, Load, multiplexer_1_out,
       multiplexer_2_out, multiplexer_3_out, multiplexer_4_out, odd_1_out_3, odd_2_out_3, odd_3_out_3,
       odd_4_out_3, Q0, Q1, Q2, Q3;

  and and_1 (and_1_out, Enable, Q0);
  and and_2 (and_2_out, and_1_out, Q1);
  and and_3 (and_3_out, and_2_out, Q2);
  and and_4 (Carry, and_3_out, Q3);
  odd odd_1 (.in_1(Enable), .in_2(Q0), .out_3(odd_1_out_3));
  odd odd_2 (.in_1(and_1_out), .in_2(Q1), .out_3(odd_2_out_3));
  odd odd_3 (.in_1(and_2_out), .in_2(Q2), .out_3(odd_3_out_3));
  odd odd_4 (.in_1(and_3_out), .in_2(Q3), .out_3(odd_4_out_3));
  Multiplexer #(.enable("false")) multiplexer_1 (.in0(odd_1_out_3), .in1(D0), .out(multiplexer_1_out), .sel(Load));
  Multiplexer multiplexer_2 (.in0(odd_2_out_3), .in1(D1), .out(multiplexer_2_out), .sel(Load));  // open: en
  Multiplexer multiplexer_3 (.in0(odd_3_out_3), .in1(D2), .out(multiplexer_3_out), .sel(Load));  // open: en
  Multiplexer multiplexer_4 (.in0(odd_4_out_3), .in1(D3), .out(multiplexer_4_out), .sel(Load));  // open: en
  TFF tff_1 (.mux(multiplexer_1_out), .CLK(CLK), .Q(Q0));
  TFF tff_2 (.mux(multiplexer_2_out), .CLK(CLK), .Q(Q1));
  TFF tff_3 (.mux(multiplexer_3_out), .CLK(CLK), .Q(Q2));
  TFF tff_4 (.mux(multiplexer_4_out), .CLK(CLK), .Q(Q3));
endmodule

module TFF (
  input  mux,
  input  CLK,
  output Q
);

  wire and_1_out, and_2_out, not_1_out, not_2_out, or_1_out;

  not not_1 (not_1_out, Q);
  not not_2 (not_2_out, mux);
  and and_1 (and_1_out, not_1_out, mux);
  and and_2 (and_2_out, not_2_out, Q);
  T_Flip_Flop t_ff_1 (.clk(CLK), .T(or_1_out), .Q(Q));  // open: Qn, preset, reset, en
  or or_1 (or_1_out, and_1_out, and_2_out);
endmodule

module odd (
  input  in_1,
  input  in_2,
  output out_3
);

  wire and_1_out, and_2_out, and_3_out, and_4_out;

  and and_1 (and_1_out, in_1, in_2);
  and and_2 (and_2_out, in_1, ~and_1_out);  // AND_Gate
  and and_3 (and_3_out, ~and_1_out, in_2);  // AND_Gate
  and and_4 (and_4_out, ~and_2_out, ~and_3_out);  // AND_Gate
  not not_1 (out_3, and_4_out);
endmodule
