// Logisim project 5.circ as structural Verilog: 1 circuit, main circuit main
module main (
);

  wire and_1_out, and_2_out, and_3_out, CLK, nA_nB_out, or_1_out, or_2_out, Q, t_ff_1_q, t_ff_2_q, w;

  and nA_nB (nA_nB_out, ~t_ff_1_q, ~t_ff_2_q);  // AND_Gate
  and and_1 (and_1_out, w, t_ff_1_q);
  and and_2 (and_2_out, ~w, t_ff_1_q);  // AND_Gate
  and and_3 (and_3_out, w, ~t_ff_1_q);  // AND_Gate
  or or_1 (or_1_out, nA_nB_out, and_1_out);
  or or_2 (or_2_out, and_2_out, and_3_out);
  T_Flip_Flop t_ff_1 (.clk(CLK), .T(or_1_out), .Q(t_ff_1_q));  // open: Qn, preset, reset, en
  T_Flip_Flop t_ff_2 (.clk(CLK), .T(or_2_out), .Q(t_ff_2_q));  // open: Qn, preset, reset, en
  and and_4 (Q, t_ff_1_q, t_ff_2_q);
endmodule
