// Logisim project 6.circ as structural Verilog: 1 circuit, main circuit main
module main (
);

  wire A_q, and_1_out, and_2_out, and_3_out, and_4_out, and_5_out, and_6_out, and_7_out, and_8_out,
       and_9_out, B_q, C_q, CLK, or_1_out, or_2_out, or_3_out, Q, w;

  and and_1 (and_1_out, A_q, B_q, ~C_q);  // AND_Gate
  and and_2 (and_2_out, ~A_q, B_q, w);  // AND_Gate
  and and_3 (and_3_out, B_q, C_q, ~A_q);  // AND_Gate
  and and_4 (and_4_out, B_q, ~A_q);  // AND_Gate
  and and_5 (and_5_out, C_q, ~A_q, ~B_q);  // AND_Gate
  and and_6 (and_6_out, ~A_q, ~w, ~C_q);  // AND_Gate
  and and_7 (and_7_out, w, ~A_q, ~B_q);  // AND_Gate
  and and_8 (and_8_out, C_q, ~A_q);  // AND_Gate
  and and_9 (and_9_out, ~w, B_q, ~A_q);  // AND_Gate
  or or_1 (or_1_out, and_1_out, and_2_out, and_3_out);
  or or_2 (or_2_out, and_4_out, and_5_out, and_6_out);
  or or_3 (or_3_out, and_7_out, and_8_out, and_9_out);
  D_Flip_Flop A (.clk(CLK), .D(or_1_out), .Q(A_q));  // open: Qn, preset, en, reset
  D_Flip_Flop B (.clk(CLK), .D(or_2_out), .Q(B_q));  // open: Qn, preset, en, reset
  D_Flip_Flop C (.clk(CLK), .D(or_3_out), .Q(C_q));  // open: Qn, preset, en, reset
  and and_10 (Q, A_q, ~B_q, ~C_q, w);  // AND_Gate
endmodule
