// Logisim project 7.circ as structural Verilog: 1 circuit, main circuit main
module main (
);

  wire and_1_out, and_2_out, and_3_out, and_4_out, and_5_out, and_6_out, and_7_out, and_8_out, and_9_out,
       and_10_out, and_11_out, and_12_out, and_13_out, and_14_out, and_15_out, and_16_out, and_17_out, CLK,
       d_ff_1_q, d_ff_2_q, d_ff_3_q, d_ff_4_q, or_1_out, or_2_out, or_3_out, or_4_out, or_5_out, p, w;

  and and_1 (and_1_out, ~d_ff_2_q, d_ff_3_q, ~w);  // AND_Gate
  and and_2 (and_2_out, ~d_ff_3_q, d_ff_1_q, ~w);  // AND_Gate
  and and_3 (and_3_out, ~d_ff_1_q, d_ff_2_q, d_ff_4_q, w);  // AND_Gate
  and and_4 (and_4_out, ~d_ff_2_q, ~w);  // AND_Gate
  and and_5 (and_5_out, ~d_ff_1_q, d_ff_4_q, d_ff_3_q);  // AND_Gate
  and and_6 (and_6_out, ~d_ff_3_q, d_ff_2_q, d_ff_4_q);  // AND_Gate
  and and_7 (and_7_out, ~d_ff_3_q, d_ff_2_q, w);  // AND_Gate
  and and_8 (and_8_out, ~d_ff_3_q, d_ff_1_q);  // AND_Gate
  and and_9 (and_9_out, ~d_ff_2_q, d_ff_4_q, w);  // AND_Gate
  and and_10 (and_10_out, ~d_ff_3_q, d_ff_2_q, ~w);  // AND_Gate
  and and_11 (and_11_out, d_ff_3_q, d_ff_2_q, ~d_ff_1_q, d_ff_4_q);  // AND_Gate
  and and_12 (and_12_out, ~d_ff_2_q, d_ff_4_q);  // AND_Gate
  and and_13 (and_13_out, ~d_ff_1_q, ~d_ff_3_q, w);  // AND_Gate
  and and_14 (and_14_out, ~d_ff_1_q, d_ff_4_q, w);  // AND_Gate
  and and_15 (and_15_out, ~w, ~d_ff_3_q, d_ff_2_q);  // AND_Gate
  or or_1 (or_1_out, and_1_out, and_2_out, and_3_out);
  or or_2 (or_2_out, and_4_out, and_5_out, and_6_out, and_7_out);
  or or_3 (or_3_out, and_8_out, and_9_out, and_10_out, and_11_out);
  or or_4 (or_4_out, and_12_out, and_13_out, and_14_out, and_15_out);
  D_Flip_Flop d_ff_1 (.clk(CLK), .D(or_1_out), .Q(d_ff_1_q));  // open: Qn, preset, en, reset
  D_Flip_Flop d_ff_2 (.clk(CLK), .D(or_2_out), .Q(d_ff_2_q));  // open: Qn, preset, en, reset
  D_Flip_Flop d_ff_3 (.clk(CLK), .D(or_3_out), .Q(d_ff_3_q));  // open: Qn, preset, en, reset
  D_Flip_Flop d_ff_4 (.clk(CLK), .D(or_4_out), .Q(d_ff_4_q));  // open: Qn, preset, en, reset
  and and_16 (and_16_out, ~d_ff_4_q, w, d_ff_3_q);  // AND_Gate
  and and_17 (and_17_out, ~w, d_ff_1_q, d_ff_3_q);  // AND_Gate
  or or_5 (or_5_out, and_16_out, and_17_out);
  D_Flip_Flop d_ff_5 (.clk(CLK), .D(or_5_out), .Q(p));  // open: Qn, preset, en, reset
endmodule
